// Logisim project v4 ALU 18 bit.circ as structural Verilog: 3 circuits, main circuit main
module main (
  input  c_in,
  input  [17:0] B,
  input  [17:0] A,
  input  c_in_sub,
  input  [2:0] OP_code,
  output ZERO,
  output [17:0] out_7,
  output [17:0] overflow_sum,
  output sum_carry,
  output sub_carry
);

  wire or_1_out;
  wire [4:0] dinshift;
  wire [17:0] adder_1_out, bit_extender_2_out, multiplier_1_out, nor_1_out, shifter_1_out, subtractor_1_out;

  Multiplier #(.width(18)) multiplier_1 (.a(A), .b(B), .out(multiplier_1_out));  // open: cin, cout
  Bit_Extender #(.in_width(18), .out_width(5)) bit_extender_1 (.in(B), .out(dinshift));
  Shifter #(.width(18)) shifter_1 (.in(A), .\dist (dinshift), .out(shifter_1_out));
  Adder #(.width(18)) adder_1 (.a(A), .b(B), .out(adder_1_out), .cin(c_in), .cout(sum_carry));
  Subtractor #(.width(18)) subtractor_1 (.a(A), .b(B), .out(subtractor_1_out), .bin(c_in_sub), .bout(sub_carry));
  Multiplexer #(.select(3), .width(18)) multiplexer_1 (
    .in0(multiplier_1_out), .in1(shifter_1_out), .in2(adder_1_out), .in3(subtractor_1_out), .out(out_7),
    .sel(OP_code));  // open: in4, in5, in6, in7, en
  or or_1 (or_1_out, sum_carry, sub_carry);
  assign bit_extender_2_out = {{17{1'b0}}, or_1_out};  // Bit_Extender bit_extender_2
  assign nor_1_out = ~(out_7 | bit_extender_2_out);  // NOR_Gate nor_1, 18 bits wide
  assign overflow_sum = out_7 ^ bit_extender_2_out;  // XOR_Gate xor_1, 18 bits wide
  Bit_Extender #(.in_width(18), .out_width(1)) bit_extender_3 (.in(nor_1_out), .out(ZERO));

  // Notes on the sheet:
  //   result
endmodule

module _16_bit_alu (
  input  [1:0] in_1,
  input  in_2,
  input  [17:0] B,
  input  [17:0] A,
  output carry_out,
  output [17:0] Overflow,
  output [17:0] result,
  output [17:0] zero,
  output Mult_carry_out,
  output sub_carry_out
);

  wire main_1_p4, main_1_p11, main_1_p12, main_2_p4, main_2_p11, main_2_p12, main_3_p4, main_3_p11,
       main_3_p12, main_4_p4, main_4_p11, main_4_p12, main_5_p4, main_5_p11, main_5_p12, main_6_p4,
       main_6_p11, main_6_p12, main_7_p4, main_7_p11, main_7_p12, main_8_p4, main_8_p11, main_8_p12,
       main_9_p4, main_9_p11, main_9_p12, main_10_p4, main_10_p11, main_10_p12, main_11_p4, main_11_p11,
       main_11_p12, main_12_p4, main_12_p11, main_12_p12, main_13_p4, main_13_p11, main_13_p12, main_14_p4,
       main_14_p11, main_14_p12, main_15_p4, main_15_p11, main_15_p12, main_16_p4, main_16_p11, main_16_p12,
       main_17_p4, main_17_p11, main_17_p12;

  // main main_1: pin names not known; wires that end beside it: B[0], A[0], in_2, main_1_p4, in_2, in_1, in_2, Overflow[0], zero[0], result[0], main_1_p11, main_1_p12
  // main main_2: pin names not known; wires that end beside it: B[1], A[1], main_1_p4, main_2_p4, main_1_p12, in_1, main_1_p11, Overflow[1], zero[1], result[1], main_2_p11, main_2_p12
  // main main_3: pin names not known; wires that end beside it: B[2], A[2], main_2_p4, main_3_p4, main_2_p12, in_1, main_2_p11, Overflow[2], zero[2], result[2], main_3_p11, main_3_p12
  // main main_4: pin names not known; wires that end beside it: B[3], A[3], main_3_p4, main_4_p4, main_3_p12, in_1, main_3_p11, Overflow[3], zero[3], result[3], main_4_p11, main_4_p12
  // main main_5: pin names not known; wires that end beside it: B[4], A[4], main_4_p4, main_5_p4, main_4_p12, in_1, main_4_p11, Overflow[4], zero[4], result[4], main_5_p11, main_5_p12
  // main main_6: pin names not known; wires that end beside it: B[5], A[5], main_5_p4, main_6_p4, main_5_p12, in_1, main_5_p11, Overflow[5], zero[5], result[5], main_6_p11, main_6_p12
  // main main_7: pin names not known; wires that end beside it: B[6], A[6], main_6_p4, main_7_p4, main_6_p12, in_1, main_6_p11, Overflow[6], zero[6], result[6], main_7_p11, main_7_p12
  // main main_8: pin names not known; wires that end beside it: B[7], A[7], main_7_p4, main_8_p4, main_7_p12, in_1, main_7_p11, Overflow[7], zero[7], result[7], main_8_p11, main_8_p12
  // main main_9: pin names not known; wires that end beside it: B[8], A[8], main_8_p4, main_9_p4, main_8_p12, in_1, main_8_p11, Overflow[8], zero[8], result[8], main_9_p11, main_9_p12
  // main main_10: pin names not known; wires that end beside it: B[9], A[9], main_9_p4, main_10_p4, main_9_p12, in_1, main_9_p11, Overflow[9], zero[9], result[9], main_10_p11, main_10_p12
  // main main_11: pin names not known; wires that end beside it: B[10], A[10], main_10_p4, main_11_p4, main_10_p12, in_1, main_10_p11, Overflow[10], zero[10], result[10], main_11_p11, main_11_p12
  // main main_12: pin names not known; wires that end beside it: B[11], A[11], main_11_p4, main_12_p4, main_11_p12, in_1, main_11_p11, Overflow[11], zero[11], result[11], main_12_p11, main_12_p12
  // main main_13: pin names not known; wires that end beside it: B[12], A[12], main_12_p4, main_13_p4, main_12_p12, in_1, main_12_p11, Overflow[12], zero[12], result[12], main_13_p11, main_13_p12
  // main main_14: pin names not known; wires that end beside it: B[13], A[13], main_13_p4, main_14_p4, main_13_p12, in_1, main_13_p11, Overflow[13], zero[13], result[13], main_14_p11, main_14_p12
  // main main_15: pin names not known; wires that end beside it: B[14], A[14], main_14_p4, main_15_p4, main_14_p12, in_1, main_14_p11, Overflow[14], zero[14], result[14], main_15_p11, main_15_p12
  // main main_16: pin names not known; wires that end beside it: B[15], A[15], main_15_p4, main_16_p4, main_15_p12, in_1, main_15_p11, Overflow[15], zero[15], result[15], main_16_p11, main_16_p12
  // main main_17: pin names not known; wires that end beside it: B[16], A[16], main_16_p4, main_17_p4, main_16_p12, in_1, main_16_p11, Overflow[16], zero[16], result[16], main_17_p11, main_17_p12
  // main main_18: pin names not known; wires that end beside it: B[17], A[17], main_17_p4, sub_carry_out, main_17_p12, in_1, main_17_p11, Overflow[17], zero[17], result[17], carry_out, Mult_carry_out
endmodule

module mult (
  output A17,
  output A16,
  output A15,
  output A14,
  output A13,
  output A12,
  output A11,
  output A0,
  output A1,
  output A2,
  output A3,
  output A4,
  output A5,
  output A6,
  output A7,
  output A8,
  output A9,
  output A10
);
endmodule
