// Logisim project v4 Control Unit.circ as structural Verilog: 1 circuit, main circuit main
module main (
  input  _1,
  input  B,
  input  A,
  output R_D,
  output R_W,
  output R_I,
  output SW,
  output SL,
  output LW,
  output Res_Mem,
  output Cu_aluClt,
  output Cu_BNE,
  output ALU_OP1,
  output ALU_OP0
);

  wire and_1_out, and_2_out, not_1_out;

  not not_1 (not_1_out, B);
  not not_2 (R_W, A);
  and and_1 (and_1_out, R_W, B);
  and and_2 (and_2_out, A, not_1_out);
  and and_3 (R_D, R_W, not_1_out);
  or or_1 (R_I, and_1_out, and_2_out);
  or or_2 (Cu_aluClt, B, A);
  and and_4 (ALU_OP0, A, B);

  assign ALU_OP1 = _1;
  assign Cu_BNE = ALU_OP0;
  assign LW = B;
  assign Res_Mem = B;
  assign SL = Cu_aluClt;
  assign SW = A;
endmodule
