// Logisim project v5 Control Unit.circ as structural Verilog: 1 circuit, main circuit main
module main (
  input  C,
  input  B,
  input  A,
  output R_D,
  output R_W,
  output R_I,
  output SW,
  output SL,
  output LW,
  output Res_Mem,
  output Cu_aluClt,
  output Cu_BNE,
  output ALU_OP2,
  output ALU_OP1,
  output ALU_OP0,
  output Jump
);

  wire and_1_out, and_2_out, and_3_out, and_5_out, and_6_out, not_1_out;

  not not_1 (not_1_out, C);
  not not_2 (R_W, B);
  not not_3 (ALU_OP1, A);
  and and_1 (and_1_out, ALU_OP1, B);
  and and_2 (and_2_out, R_W, C);
  and and_3 (and_3_out, ALU_OP1, C);
  and and_4 (LW, ALU_OP1, C);
  and and_5 (and_5_out, ALU_OP1, B);
  and and_6 (and_6_out, R_W, C);
  and and_7 (R_D, ALU_OP1, R_W, not_1_out);
  or or_1 (R_I, and_1_out, and_2_out);
  or or_2 (SW, ALU_OP1, B);
  or or_3 (SL, SW, and_3_out);
  or or_4 (Cu_aluClt, and_5_out, and_6_out);
  and and_8 (Cu_BNE, ALU_OP1, B, C);
  and and_9 (ALU_OP2, ALU_OP1, R_W);
  and and_10 (ALU_OP0, ALU_OP1, B, C);
  and and_11 (Jump, A, R_W, not_1_out);

  assign Res_Mem = LW;
endmodule
