// Logisim project v5 Main 18 bit.circ as structural Verilog: 1 circuit, main circuit main
module main (
  input  in_1,
  input  in_2,
  input  in_3,
  input  in_4,
  input  in_5,
  output [17:0] Instructions,
  output [4:0] _16_8_4_2_1,
  output [3:0] RD__Immediate,
  output [3:0] RT,
  output [3:0] RS,
  output [17:0] Data_Read_2,
  output [3:0] OP,
  output [17:0] Output,
  output [1:0] Function,
  output [17:0] Data_Read_1,
  output [17:0] Instructions_2,
  output [17:0] Address,
  output [7:0] out_18,
  output [17:0] overflow
);

  wire and_1_out, bit_extender_8_out, clk, cu_aluClt, J, lw, main_2_zero, main_3_cu_beq__cd, R_I, R_W,
       Res_Mem, RT_RD, sl, sw;
  wire [2:0] AluOp, bit_extender_7_out, multiplexer_4_out;
  wire [3:0] multiplexer_2_out;
  wire [6:0] adder_1_out, adder_2_out, bit_extender_1_out, bit_extender_2_out, shifter_1_out, shifter_2_out;
  wire [7:0] bit_extender_3_out, bit_extender_4_out;
  wire [17:0] adder_3_out, Address_t, bit_extender_6_out, cu_bne, main_4_out_7, multiplexer_3_out,
       multiplexer_5_out, ram_1_data, register_1_q, shifter_4_out;

  assign bit_extender_1_out = {{3{1'b0}}, Instructions_2[3:0]};  // Bit_Extender bit_extender_1
  assign bit_extender_2_out = {{5{1'b0}}, Function};  // Bit_Extender bit_extender_2
  Register #(.width(18)) register_1 (.D(Address_t), .Q(register_1_q), .clk(clk), .clr(in_4));  // open: en
  Clock clock_1 (.out(clk));
  Shifter #(.width(7)) shifter_1 (.in(bit_extender_1_out), .\dist (3'b100), .out(shifter_1_out));
  Shifter #(.width(7)) shifter_2 (.in(7'b0000011), .\dist (3'b101), .out(shifter_2_out));
  Adder #(.width(7)) adder_1 (.a(shifter_1_out), .b(bit_extender_2_out), .out(adder_1_out));  // open: cin, cout
  Adder #(.width(7)) adder_2 (.a(shifter_2_out), .b(7'b0000100), .out(adder_2_out));  // open: cin, cout
  Adder #(.width(18)) adder_3 (.a(register_1_q), .b(18'h1), .out(adder_3_out));  // open: cin, cout
  ROM #(.addrWidth(18), .dataWidth(18)) rom_1 (
    .addr(register_1_q), .data({Function, Instructions_2[15:0]}));  // open: sel
  assign bit_extender_3_out = {{1{1'b0}}, adder_1_out};  // Bit_Extender bit_extender_3
  assign bit_extender_4_out = {{1{1'b0}}, adder_2_out};  // Bit_Extender bit_extender_4
  Multiplexer #(.width(8), .enable("false")) multiplexer_1 (
    .in0(bit_extender_3_out), .in1(bit_extender_4_out), .out(out_18), .sel(in_5));
  assign _16_8_4_2_1 = {{1{1'b0}}, Instructions_2[7:4]};  // Bit_Extender bit_extender_5
  Shifter #(.width(18), .shift("lr")) shifter_3 (
    .in({Function, 4'b0000, Instructions_2[11:0]}), .\dist (_16_8_4_2_1), .out(Instructions));
  Multiplexer #(.width(4), .enable("false")) multiplexer_2 (
    .in0(Instructions_2[7:4]), .in1(Instructions_2[3:0]), .out(multiplexer_2_out), .sel(RT_RD));
  assign bit_extender_6_out = {{10{1'b0}}, out_18};  // Bit_Extender bit_extender_6
  // v3_REG_18_bit__main main_1: pin names not known; wires that end beside it: Instructions_2[11:8], Instructions_2[7:4], multiplexer_2_out, Output, clk, R_W, Data_Read_1, Data_Read_2
  assign bit_extender_7_out = {{1{1'b0}}, Function};  // Bit_Extender bit_extender_7
  Multiplexer #(.width(18), .enable("false")) multiplexer_3 (
    .in0(Data_Read_2), .in1(bit_extender_6_out), .out(multiplexer_3_out), .sel(R_I));
  Multiplexer #(.width(3), .enable("false")) multiplexer_4 (
    .in0(bit_extender_7_out), .in1(AluOp), .out(multiplexer_4_out), .sel(cu_aluClt));
  Shifter #(.width(18)) shifter_4 (.in(bit_extender_6_out), .\dist (5'b00001), .out(shifter_4_out));
  Bit_Extender #(.in_width(18), .out_width(1)) bit_extender_8 (.in(cu_bne), .out(bit_extender_8_out));
  v4_ALU_18_bit_main main_2 (
    .ZERO(main_2_zero), .out_7(Address), .overflow_sum(overflow), .c_in(in_2), .A(Data_Read_1),
    .B(multiplexer_3_out), .OP_code(multiplexer_4_out));  // open: sum_carry, c_in_sub, sub_carry
  and and_1 (and_1_out, bit_extender_8_out, main_2_zero);
  v6_Control_Unit_main main_3 (
    .RT_RD__B_prime_C_prime_D_prime(RT_RD), .D(Instructions_2[12]), .C(Instructions_2[13]),
    .B(Instructions_2[14]), .A(Instructions_2[15]), .R_W__C_prime(R_W), .R_I__C_D(R_I), .SW__CD_prime(sw),
    .SL__B_prime_C_prime_D_CD_prime(sl), .LW__B_prime_C_prime_D(lw), .RES_MEM__B_prime_D(Res_Mem),
    .ALU_OP_2(AluOp[2]), .ALU_OP_1__A_prime(AluOp[1]), .ALU_OP_0__CD(AluOp[0]),
    .CU_BEQ__CD(main_3_cu_beq__cd), .CU_AluClt__C_D(cu_aluClt), .Jump__A_prime_BD_prime(J));
  v4_ALU_18_bit_main main_4 (
    .out_7(main_4_out_7), .c_in(in_1), .A(adder_3_out), .B(shifter_4_out), .OP_code(3'b010));  // open: ZERO, overflow_sum, sum_carry, c_in_sub, sub_carry
  assign cu_bne = {{17{1'b0}}, main_3_cu_beq__cd};  // Bit_Extender bit_extender_9
  Multiplexer #(.width(18), .enable("false")) multiplexer_5 (
    .in0(adder_3_out), .in1(main_4_out_7), .out(multiplexer_5_out), .sel(and_1_out));
  Multiplexer #(.width(18), .enable("false")) multiplexer_6 (
    .in0(Address), .in1(ram_1_data), .out(Output), .sel(Res_Mem));
  RAM #(.addrWidth(18), .dataWidth(18), .bus("separate")) ram_1 (
    .addr(Address), .din(Data_Read_2), .data(ram_1_data), .str(sw), .sel(sl), .clk(clk), .ld(lw), .clr(in_3));
  Multiplexer #(.width(18), .enable("false")) multiplexer_7 (
    .in0(multiplexer_5_out), .in1(Instructions), .out(Address_t), .sel(J));

  assign Instructions_2[17:16] = Function;
  assign OP = Instructions_2[15:12];
  assign RD__Immediate = Instructions_2[3:0];
  assign RS = Instructions_2[11:8];
  assign RT = Instructions_2[7:4];

  // Other names for the same wires on the sheet: RD[3:0] = Instructions_2[3:0]; D_in[17:0] = Output;
  //   Imm[7:0] = out_18; cu_[3:0] = Instructions_2[15:12]

  // Notes on the sheet:
  //   contents of rom_1 (hex, n*v repeats v):
  //   3504e 5030 0 0 23340 2300 15330 4270 0 5030 35040 5050 23340 2330 15330 4670 5030 5030 0 0 23340
  //   1310 20515 4d70
  //   3000e -> for 99 
endmodule
