// Logisim project v6 Control Unit.circ as structural Verilog: 2 circuits, main circuit main
module main (
  input  D,
  input  C,
  input  B,
  input  A,
  output RT_RD__B_prime_C_prime_D_prime,
  output R_W__C_prime,
  output R_I__C_D,
  output SW__CD_prime,
  output SL__B_prime_C_prime_D_CD_prime,
  output LW__B_prime_C_prime_D,
  output RES_MEM__B_prime_D,
  output ALU_OP_2,
  output ALU_OP_1__A_prime,
  output ALU_OP_0__CD,
  output CU_BEQ__CD,
  output CU_AluClt__C_D,
  output Jump__A_prime_BD_prime
);

  wire and_2_out, and_4_out, and_5_out, not_1_out, not_3_out;

  not not_1 (not_1_out, D);
  not not_2 (R_W__C_prime, C);
  not not_3 (not_3_out, B);
  not not_4 (ALU_OP_1__A_prime, A);
  and and_1 (RT_RD__B_prime_C_prime_D_prime, not_3_out, R_W__C_prime, not_1_out);
  and and_2 (and_2_out, C, not_1_out);
  and and_3 (SW__CD_prime, C, not_1_out);
  and and_4 (and_4_out, not_3_out, R_W__C_prime, D);
  and and_5 (and_5_out, C, not_1_out);
  and and_6 (LW__B_prime_C_prime_D, not_3_out, R_W__C_prime, D);
  and and_7 (RES_MEM__B_prime_D, not_3_out, D);
  and and_8 (ALU_OP_0__CD, C, D);
  or or_1 (CU_AluClt__C_D, C, D);
  and and_9 (Jump__A_prime_BD_prime, ALU_OP_1__A_prime, B, not_1_out);
  or or_2 (SL__B_prime_C_prime_D_CD_prime, and_4_out, and_5_out);
  or or_3 (R_I__C_D, and_2_out, B);

  assign ALU_OP_2 = 1'b0;
  assign CU_BEQ__CD = ALU_OP_0__CD;
endmodule

module test (
  input  D_C_B_A,
  input  in_2,
  input  in_3,
  input  in_4,
  output out_5,
  output out_6,
  output out_7,
  output out_8,
  output out_9,
  output out_10,
  output out_11,
  output out_12,
  output out_13,
  output out_14,
  output out_15,
  output out_16,
  output out_17
);

  main main_1 (
    .RT_RD__B_prime_C_prime_D_prime(out_5), .D(in_4), .C(in_3), .B(in_2), .A(D_C_B_A), .R_W__C_prime(out_6),
    .R_I__C_D(out_7), .SW__CD_prime(out_8), .SL__B_prime_C_prime_D_CD_prime(out_9),
    .LW__B_prime_C_prime_D(out_10), .RES_MEM__B_prime_D(out_11), .ALU_OP_2(out_12),
    .ALU_OP_1__A_prime(out_13), .ALU_OP_0__CD(out_14), .CU_BEQ__CD(out_15), .CU_AluClt__C_D(out_16),
    .Jump__A_prime_BD_prime(out_17));
endmodule
